# Fritzing sketch FairyWings_Dress (saved by Fritzing 0.9.3b)
breadboards: 1

parts:
  Part2 = Adafruit Pixie [part_number="Adafruit #2741"]
  USBTTL2 = USB TTL Serial Cable
  U1 = attiny85 [package=dip]
  BAT1 = 18650 battery holder [package=battery-18650-kit]

nets:
  5V: Part2.5V, USBTTL2.5V
  N1: Part2.IN, U1.Pin_7
  GND: Part2.GND, USBTTL2.RX, USBTTL2.GND, U1.Pin_4, BAT1.-
  N2: U1.Pin_1, BAT1.+

custom parts:
  Adafruit Pixie: NeoPixels are plenty bright, suuuure. BUT ARE THEY 3 WATTS BRIGHT? No! They are not! That's why you need a Pixie. These chainable smart LEDs are not only super-smart, they are ridonkulously bright with 3W total, compared to 0.2W of a 'standard' NeoPixel. Designed by Ytai Ben-Tsvi, these are the ultimate in LEDs.
  18650 battery holder: 18650 Battery Holder
