# Fritzing sketch TinyRotayPCB (saved by Fritzing 0.9.3b)
circuit board: 8.46667cm x 5.64444cm
perfboards: 1

parts:
  ATTINY85 = attiny85 [package=dip]
  ENCODER1 = Rotary Encoder with Knob
  J1 = rounded female pin header, 4 pins [form="♀ (female rounded)"]
  J2 = rounded female pin header, 4 pins [form="♀ (female rounded)"]
  R2 = Resistor [tolerance=±5% resistance=220 package=THT]
  R1 = Resistor [tolerance=±5% resistance=220 package=THT]
  Batt = Header 2 [package=molex-1x2_lock]
  BAT1 = Battery Holders [package=battery-aaa]
  BAT2 = Battery Holders [package=battery-aaa]
  BAT3 = Battery Holders [package=battery-aaa]
  BAT4 = Battery Holders [package=battery-aaa]
  S1 = SPST Switch [package=switch-spdt_lock.007s]
  Out2 = male pin header, 3 pins [form="♂ (male)"]
  Batt_2 = male pin header, 2 pins [form="♂ (male)"]
  Switch = male pin header, 2 pins [form="♂ (male)"]
  Out1 = male pin header, 3 pins [form="♂ (male)"]
  Switch_2 = Header 2 [package=molex-1x2_lock]

nets:
  N1: ATTINY85.Pin_1, J1.pin1
  N2: ATTINY85.Pin_2, ENCODER1.no_name_yet#3, J1.pin2
  N3: ATTINY85.Pin_3, ENCODER1.no_name_yet#1, J1.pin3
  N4: ATTINY85.Pin_4, ENCODER1.no_name_yet#2, ENCODER1.no_name_yet#5, J1.pin4, Batt.1, BAT4.-, Out2.pin3, Batt_2.pin1, Out1.pin3
  N5: ATTINY85.Pin_5, J2.pin1, R1.Pin_0
  N6: ATTINY85.Pin_6, J2.pin2, R2.Pin_0
  N7: ATTINY85.Pin_7, ENCODER1.no_name_yet#4, J2.pin3
  N8: ATTINY85.Pin_8, J2.pin4, S1.P, Out2.pin1, Switch.pin1, Out1.pin1, Switch_2.1
  N9: R2.Pin_1, Out2.pin2
  N10: R1.Pin_1, Out1.pin2
  N11: Batt.2, BAT2.+, S1.O, Batt_2.pin2, Switch.pin2, Switch_2.2
  N12: BAT1.-, BAT3.+
  N13: BAT1.+, BAT2.-
  N14: BAT3.-, BAT4.+

custom parts:
  Rotary Encoder with Knob: Rotary Encoder with 1/4" Shaft and Knob
